# Fritzing sketch RadarCircuit (saved by Fritzing 0.9.3b)
breadboards: 1
stripboards: 1

parts:
  Part1 = Adafruit Feather M0 RFM9x LoRa [part_number="Adafruit #3178 or #3179"]
  J3 = Generic male header - 5 pins [form="♂ (male)" package=THT]
  R1 = Resistor [tolerance=±5% resistance=220 package=THT]
  R2 = Resistor [tolerance=±5% resistance=220 package=THT]
  LED1 = LED - 5mm [color="Green (565nm)" package="5 mm [THT]"]
  LED2 = LED - 5mm [color="Red (635nm)" package="5 mm [THT]"]
  LED3 = LED - 5mm [color="Blue (470nm)" package="5 mm [THT]"]
  R3 = Resistor [tolerance=±5% resistance=220 package=THT]
  Part2 = Logic Level Converter

nets:
  N1: Part1.D1, R2.Pin_0
  N2: Part1.D0, R1.Pin_0
  GND: Part1.GND, J3.GND, LED1.anode, LED2.anode, LED3.anode, Part2.GND
  N3: Part1.+3V3, Part2.LV
  N4: Part1.D13, J3.OUT
  N5: Part1.D5, R3.Pin_0
  N6: J3.VIN, Part2.HV
  N7: R1.Pin_1, LED1.cathode
  N8: R2.Pin_1, LED2.cathode
  N9: LED3.cathode, R3.Pin_1

custom parts:
  Adafruit Feather M0 RFM9x LoRa: This is the Adafruit Feather M0 RFM95 LoRa Radio - our take on an microcontroller with a "Long Range (LoRa)" packet radio transceiver with built in USB and battery charging. Its an Adafruit Feather M0 with a 433Mhz or 900MHz radio module cooked in! Great for making wireless networks that are more flexible than Bluetooth LE and without the high power requirements of WiFi. We have other boards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
  Generic male header - 5 pins: Generic male header
